// Logisim project new_stack.circ as structural Verilog: 10 circuits, main circuit main
module main (
  input  start,
  input  clk,
  input  reset,
  input  pushin,
  input  [15:0] mem_data_in,
  output [15:0] mem_data
);

  core core_1 (.start(start), .clk(clk), .reset(reset), .pushin(pushin), .data(mem_data_in), .out_6(mem_data));
endmodule

module mux2_1 (
  input  [15:0] B,
  input  [15:0] A,
  input  selector,
  output [15:0] outt
);

  Multiplexer #(.width(16), .enable("false")) multiplexer_1 (.in0(B), .in1(A), .out(outt), .sel(selector));
endmodule

module mux4_2 (
  input  [15:0] a,
  input  [15:0] b,
  input  [15:0] c,
  input  [15:0] d,
  input  [1:0] SELECTS,
  output [15:0] OUTT
);

  Multiplexer #(.select(2), .width(16), .enable("false")) multiplexer_1 (
    .in0(a), .in1(b), .in2(c), .in3(d), .out(OUTT), .sel(SELECTS));
endmodule

module bufferS (
  input  [15:0] INN,
  input  ENABLE,
  output [15:0] OUTT
);

  assign OUTT = ENABLE ? INN : 16'bz;  // Controlled_Buffer controlled_buffer_1
endmodule

module ALU (
  input  A,
  input  B,
  input  [15:0] Aluin,
  input  C,
  input  clk,
  input  reset,
  output [15:0] o_tos
);

  wire [15:0] adder_1_out, and_1_out, divider_1_out, multiplexer_1_out, multiplexer_2_out, multiplexer_3_out,
       multiplier_1_out, negator_1_out, not_1_out, or_1_out, register_1_q, register_2_q, register_3_q,
       shifter_1_out, shifter_2_out, subtractor_1_out, undriven, xor_1_out;

  Multiplexer #(.width(16), .enable("false")) multiplexer_1 (
    .in0(register_1_q), .in1(Aluin), .out(multiplexer_1_out), .sel(A));
  Multiplexer #(.width(16), .enable("false")) multiplexer_2 (
    .in0(register_2_q), .in1(Aluin), .out(multiplexer_2_out), .sel(B));
  Multiplexer #(.width(16), .enable("false")) multiplexer_3 (
    .in0(register_3_q), .in1(Aluin), .out(multiplexer_3_out), .sel(C));
  Register #(.width(16)) register_1 (.D(multiplexer_1_out), .clk(clk), .Q(register_1_q), .clr(reset));  // open: en
  Register #(.width(16)) register_2 (.D(multiplexer_2_out), .clk(clk), .Q(register_2_q), .clr(reset));  // open: en
  Register #(.width(16)) register_3 (.D(multiplexer_3_out), .clk(clk), .Q(register_3_q), .clr(reset));  // open: en
  assign or_1_out = register_1_q | register_2_q;  // OR_Gate or_1, 16 bits wide
  assign xor_1_out = register_1_q ^ register_2_q;  // XOR_Gate xor_1, 16 bits wide
  assign and_1_out = register_1_q & register_2_q;  // AND_Gate and_1, 16 bits wide
  Shifter #(.width(16)) shifter_1 (.in(register_1_q), .\dist (register_2_q[3:0]), .out(shifter_1_out));
  Shifter #(.width(16), .shift("lr")) shifter_2 (.in(register_1_q), .\dist (register_2_q[3:0]), .out(shifter_2_out));
  Adder #(.width(16)) adder_1 (.a(register_1_q), .b(register_2_q), .out(adder_1_out));  // open: cin, cout
  Subtractor #(.width(16)) subtractor_1 (
    .a(register_1_q), .b(register_2_q), .out(subtractor_1_out));  // open: bin, bout
  Multiplier #(.width(16)) multiplier_1 (
    .a(register_1_q), .b(register_2_q), .out(multiplier_1_out));  // open: cin, cout
  Negator #(.width(16)) negator_1 (.in(register_2_q), .out(negator_1_out));
  Divider #(.width(16)) divider_1 (.a(register_1_q), .b(register_2_q), .out(divider_1_out));  // open: upper, rem
  assign not_1_out = ~register_1_q;  // NOT_Gate not_1, 16 bits wide
  Multiplexer #(.select(4), .width(16), .enable("false")) multiplexer_4 (
    .in0(register_1_q), .in1(or_1_out), .in2(xor_1_out), .in3(and_1_out), .in4(shifter_1_out),
    .in5(shifter_2_out), .in6(adder_1_out), .in7(subtractor_1_out), .in8(multiplier_1_out),
    .in9(negator_1_out), .in10(divider_1_out), .in11(not_1_out), .in12(undriven), .in13(undriven),
    .in14(undriven), .in15(undriven), .out(o_tos), .sel(register_3_q[3:0]));
endmodule

module stack (
  input  push,
  input  pop,
  input  rst,
  input  clk,
  input  [15:0] Ain,
  output [4:0] tos_position,
  output [15:0] Aout
);

  wire multiplexer_2_out;
  wire [4:0] adder_1_out, multiplexer_1_out, multiplexer_3_out, multiplexer_4_out, subtractor_1_out;

  Multiplexer #(.width(5), .enable("false")) multiplexer_1 (
    .in0(subtractor_1_out), .in1(tos_position), .out(multiplexer_1_out), .sel(push));
  RAM #(.addrWidth(5), .dataWidth(16), .databus("bibus")) ram_1 (
    .addr(multiplexer_1_out), .we(multiplexer_2_out), .clk(clk), .din(Ain), .dout(Aout));  // open: oe
  Multiplexer #(.enable("false")) multiplexer_2 (.in0(1'b0), .in1(1'b1), .out(multiplexer_2_out), .sel(push));
  Adder #(.width(5)) adder_1 (.a(tos_position), .b(5'b00001), .out(adder_1_out));  // open: cin, cout
  Subtractor #(.width(5)) subtractor_1 (.a(tos_position), .b(5'b00001), .out(subtractor_1_out));  // open: bin, bout
  Multiplexer #(.width(5), .enable("false")) multiplexer_3 (
    .in0(tos_position), .in1(adder_1_out), .out(multiplexer_3_out), .sel(push));
  Multiplexer #(.width(5), .enable("false")) multiplexer_4 (
    .in0(multiplexer_3_out), .in1(subtractor_1_out), .out(multiplexer_4_out), .sel(pop));
  Register #(.width(5)) register_1 (.D(multiplexer_4_out), .clk(clk), .Q(tos_position), .clr(rst));  // open: en
endmodule

module data_path (
  input  data_push,
  input  data_pop,
  input  A,
  input  B,
  input  C,
  input  r_push,
  input  r_pop,
  input  rst,
  input  clk,
  input  [15:0] datain,
  input  [1:0] d_select,
  output [4:0] PosA,
  output [15:0] alu_out,
  output [4:0] PosB,
  output [15:0] Ain
);

  wire [15:0] stack_1_aout, stack_2_aout;

  stack stack_1 (
    .push(data_push), .pop(data_pop), .rst(rst), .clk(clk), .Ain(Ain), .tos_position(PosA),
    .Aout(stack_1_aout));
  stack stack_2 (
    .push(r_push), .pop(r_pop), .rst(rst), .clk(clk), .Ain(stack_1_aout), .tos_position(PosB),
    .Aout(stack_2_aout));
  ALU alu_1 (.A(A), .B(B), .Aluin(stack_1_aout), .C(C), .clk(clk), .reset(rst), .o_tos(alu_out));
  mux4_2 mux4_2_1 (.a(datain), .b(alu_out), .c(stack_2_aout), .d(stack_1_aout), .SELECTS(d_select), .OUTT(Ain));
endmodule

module control (
  input  start,
  input  [4:0] PosA,
  input  [4:0] PosB,
  input  [15:0] Ain,
  input  clk,
  input  reset,
  output [4:0] out_7,
  output [1:0] d_select,
  output pushA,
  output popA,
  output AluA,
  output AluB,
  output AluSel,
  output PushB,
  output PopB
);

  wire and_1_out, and_2_out, and_3_out, and_4_out, and_5_out, and_6_out, and_7_out, and_8_out, and_9_out,
       and_10_out, and_11_out, and_12_out, comparator_1_gt, comparator_2_gt, comparator_3_eq,
       comparator_4_eq, comparator_5_eq, comparator_6_eq, comparator_7_eq, comparator_8_eq, comparator_9_eq,
       comparator_10_eq, comparator_11_gt, multiplexer_6_out, multiplexer_7_out, multiplexer_10_out,
       multiplexer_11_out, multiplexer_14_out, multiplexer_16_out, multiplexer_17_out, multiplexer_22_out,
       multiplexer_23_out, or_1_out, or_2_out, register_2_q, register_3_q, register_5_q, register_6_q,
       register_10_q;
  wire [1:0] multiplexer_1_out, multiplexer_2_out, multiplexer_3_out, multiplexer_4_out, multiplexer_8_out,
       multiplexer_9_out;
  wire [4:0] adder_1_out, multiplexer_5_out, multiplexer_13_out, subtractor_1_out;
  wire [15:0] multiplexer_12_out, register_9_q;

  Subtractor #(.width(5)) subtractor_1 (.a(out_7), .b(5'b00001), .out(subtractor_1_out));  // open: bin, bout
  Adder #(.width(5)) adder_1 (.a(out_7), .b(5'b00001), .out(adder_1_out));  // open: cin, cout
  Comparator #(.width(5)) comparator_1 (.a(out_7), .b(5'b00001), .gt(comparator_1_gt));  // open: eq, lt
  Comparator #(.width(5)) comparator_2 (.a(out_7), .b(5'b00011), .gt(comparator_2_gt));  // open: eq, lt
  Comparator #(.width(5)) comparator_3 (.a(PosB), .b({5{1'b0}}), .eq(comparator_3_eq));  // open: gt, lt
  Multiplexer #(.width(2), .enable("false")) multiplexer_1 (
    .in0(2'b01), .in1(2'b10), .out(multiplexer_1_out), .sel(subtractor_1_out[0]));
  Multiplexer #(.width(2), .enable("false")) multiplexer_2 (
    .in0(2'b00), .in1(2'b00), .out(multiplexer_2_out), .sel(subtractor_1_out[0]));
  Multiplexer #(.select(2), .width(2), .enable("false")) multiplexer_3 (
    .in0(2'b01), .in1(2'b10), .in2(2'b00), .in3(2'b00), .out(multiplexer_3_out), .sel(subtractor_1_out[1:0]));
  Multiplexer #(.select(2), .width(2), .enable("false")) multiplexer_4 (
    .in0(2'b00), .in1(2'b00), .in2(2'b00), .in3(2'b00), .out(multiplexer_4_out), .sel(subtractor_1_out[1:0]));
  Comparator #(.width(5)) comparator_4 (.a(PosA), .b({5{1'b1}}), .eq(comparator_4_eq));  // open: gt, lt
  and and_1 (and_1_out, ~popA, register_6_q);  // AND_Gate
  and and_2 (and_2_out, ~pushA, register_10_q, register_5_q);  // AND_Gate
  or or_1 (or_1_out, and_1_out, and_2_out, and_3_out);
  and and_3 (and_3_out, ~pushA, ~register_6_q, ~popA, ~register_5_q);  // AND_Gate
  Multiplexer #(.width(5), .enable("false")) multiplexer_5 (
    .in0(out_7), .in1(adder_1_out), .out(multiplexer_5_out), .sel(start));
  Multiplexer #(.enable("false")) multiplexer_6 (
    .in0(comparator_1_gt), .in1(comparator_2_gt), .out(multiplexer_6_out), .sel(or_2_out));
  or or_2 (or_2_out, popA, register_2_q);
  Comparator #(.width(5)) comparator_5 (.a(PosA), .b({5{1'b0}}), .eq(comparator_5_eq));  // open: gt, lt
  Multiplexer #(.enable("false")) multiplexer_7 (
    .in0(register_3_q), .in1(comparator_3_eq), .out(multiplexer_7_out), .sel(and_4_out));
  Multiplexer #(.width(2), .enable("false")) multiplexer_8 (
    .in0(multiplexer_1_out), .in1(multiplexer_2_out), .out(multiplexer_8_out), .sel(register_3_q));
  Multiplexer #(.width(2), .enable("false")) multiplexer_9 (
    .in0(multiplexer_3_out), .in1(multiplexer_4_out), .out(multiplexer_9_out), .sel(register_3_q));
  Multiplexer #(.enable("false")) multiplexer_10 (
    .in0(pushA), .in1(1'b0), .out(multiplexer_10_out), .sel(multiplexer_6_out));
  and and_4 (and_4_out, ~comparator_4_eq, or_1_out);  // AND_Gate
  Multiplexer #(.enable("false")) multiplexer_11 (
    .in0(popA), .in1(1'b0), .out(multiplexer_11_out), .sel(multiplexer_6_out));
  and and_5 (and_5_out, register_5_q, ~register_10_q, ~pushA);  // AND_Gate
  and and_6 (and_6_out, register_6_q, ~popA);  // AND_Gate
  and and_7 (and_7_out, and_6_out, comparator_6_eq);
  Comparator #(.width(5)) comparator_6 (.a(out_7), .b({5{1'b0}}), .eq(comparator_6_eq));  // open: gt, lt
  and and_8 (and_8_out, popA, comparator_7_eq);
  Comparator #(.width(5)) comparator_7 (.a(out_7), .b(5'b00011), .eq(comparator_7_eq));  // open: gt, lt
  and and_9 (and_9_out, popA, comparator_8_eq);
  Comparator #(.width(5)) comparator_8 (.a(out_7), .b(5'b00100), .eq(comparator_8_eq));  // open: gt, lt
  Comparator #(.width(5)) comparator_9 (.a(out_7), .b(5'b00010), .eq(comparator_9_eq));  // open: gt, lt
  and and_10 (and_10_out, comparator_9_eq, popA);
  Comparator #(.width(2)) comparator_10 (.a(d_select), .b(2'b01), .eq(comparator_10_eq));  // open: gt, lt
  and and_11 (and_11_out, comparator_10_eq, pushA);
  Multiplexer #(.width(16), .enable("false")) multiplexer_12 (
    .in0(register_9_q), .in1(Ain), .out(multiplexer_12_out), .sel(Ain[15]));
  Comparator #(.width(16), .mode("unsigned")) comparator_11 (
    .a(multiplexer_12_out), .b(register_9_q), .gt(comparator_11_gt));  // open: eq, lt
  and and_12 (and_12_out, multiplexer_6_out, pushA);
  Register #(.width(5)) register_1 (.D(multiplexer_13_out), .clk(clk), .Q(out_7), .clr(reset));  // open: en
  Multiplexer #(.width(5), .enable("false")) multiplexer_13 (
    .in0(multiplexer_5_out), .in1({5{1'b0}}), .out(multiplexer_13_out), .sel(multiplexer_6_out));
  Register #(.width(1)) register_2 (.D(multiplexer_14_out), .clk(clk), .Q(register_2_q), .clr(reset));  // open: en
  Multiplexer #(.enable("false")) multiplexer_14 (
    .in0(register_2_q), .in1(comparator_5_eq), .out(multiplexer_14_out), .sel(and_4_out));
  Register #(.width(1)) register_3 (.D(multiplexer_7_out), .clk(clk), .Q(register_3_q), .clr(reset));  // open: en
  Multiplexer #(.width(2), .enable("false")) multiplexer_15 (
    .in0(multiplexer_8_out), .in1(multiplexer_9_out), .out(d_select), .sel(or_2_out));
  Register #(.width(1)) register_4 (.D(multiplexer_16_out), .clk(clk), .Q(pushA), .clr(reset));  // open: en
  Multiplexer #(.enable("false")) multiplexer_16 (
    .in0(multiplexer_10_out), .in1(1'b1), .out(multiplexer_16_out), .sel(and_4_out));
  Register #(.width(1)) register_5 (.D(pushA), .clk(clk), .Q(register_5_q), .clr(reset));  // open: en
  Register #(.width(1)) register_6 (.D(popA), .clk(clk), .Q(register_6_q), .clr(reset));  // open: en
  Register #(.width(1)) register_7 (.D(multiplexer_17_out), .clk(clk), .Q(popA), .clr(reset));  // open: en
  Multiplexer #(.enable("false")) multiplexer_17 (
    .in0(multiplexer_11_out), .in1(1'b1), .out(multiplexer_17_out), .sel(and_5_out));
  Multiplexer #(.enable("false")) multiplexer_18 (.in0(1'b0), .in1(1'b1), .out(AluA), .sel(and_7_out));
  Multiplexer #(.enable("false")) multiplexer_19 (.in0(1'b0), .in1(1'b1), .out(AluB), .sel(and_8_out));
  Multiplexer #(.enable("false")) multiplexer_20 (.in0(1'b0), .in1(1'b1), .out(AluSel), .sel(and_9_out));
  Multiplexer #(.enable("false")) multiplexer_21 (.in0(1'b0), .in1(1'b1), .out(PushB), .sel(and_10_out));
  Register #(.width(1)) register_8 (.D(multiplexer_22_out), .clk(clk), .Q(PopB), .clr(reset));  // open: en
  Multiplexer #(.enable("false")) multiplexer_22 (.in0(1'b0), .in1(1'b1), .out(multiplexer_22_out), .sel(and_11_out));
  Register #(.width(16)) register_9 (.D(multiplexer_12_out), .clk(clk), .Q(register_9_q), .clr(reset));  // open: en
  Register #(.width(1)) register_10 (.D(multiplexer_23_out), .clk(clk), .Q(register_10_q), .clr(reset));  // open: en
  Multiplexer #(.enable("false")) multiplexer_23 (
    .in0(register_10_q), .in1(comparator_11_gt), .out(multiplexer_23_out), .sel(and_12_out));
endmodule

module core (
  input  start,
  input  clk,
  input  reset,
  input  pushin,
  input  [15:0] data,
  output [15:0] out_6
);

  wire control_1_alua, control_1_alub, control_1_alusel, control_1_popa, control_1_popb, control_1_pusha,
       control_1_pushb;
  wire [1:0] control_1_d_select;
  wire [4:0] data_path_1_posa, data_path_1_posb;
  wire [15:0] acc_in_1_reseult, data_path_1_ain;

  control control_1 (
    .start(start), .PosA(data_path_1_posa), .PosB(data_path_1_posb), .Ain(data_path_1_ain), .clk(clk),
    .reset(reset), .d_select(control_1_d_select), .pushA(control_1_pusha), .popA(control_1_popa),
    .AluA(control_1_alua), .AluB(control_1_alub), .AluSel(control_1_alusel), .PushB(control_1_pushb),
    .PopB(control_1_popb));  // open: out_7
  acc_in acc_in_1 (
    .push(pushin), .pop(control_1_pusha), .d2(control_1_d_select), .reset(reset), .clk(clk), .enter(data),
    .reseult(acc_in_1_reseult));
  data_path data_path_1 (
    .data_push(control_1_pusha), .data_pop(control_1_popa), .A(control_1_alua), .B(control_1_alub),
    .C(control_1_alusel), .r_push(control_1_pushb), .r_pop(control_1_popb), .rst(reset), .clk(clk),
    .datain(acc_in_1_reseult), .d_select(control_1_d_select), .PosA(data_path_1_posa), .alu_out(out_6),
    .PosB(data_path_1_posb), .Ain(data_path_1_ain));
endmodule

module acc_in (
  input  push,
  input  pop,
  input  [1:0] d2,
  input  reset,
  input  clk,
  input  [15:0] enter,
  output [15:0] reseult
);

  wire and_1_out, and_2_out, and_3_out, comparator_1_eq, multiplexer_3_out, register_2_q;
  wire [4:0] adder_1_out, multiplexer_1_out, multiplexer_2_out, multiplexer_4_out, multiplexer_5_out,
       multiplexer_6_out, register_1_q, subtractor_1_out, subtractor_2_out;

  Comparator #(.width(2)) comparator_1 (.a(d2), .b(2'b00), .eq(comparator_1_eq));  // open: gt, lt
  and and_1 (and_1_out, pop, comparator_1_eq);
  Adder #(.width(5)) adder_1 (.a(register_1_q), .b(5'b00001), .out(adder_1_out));  // open: cin, cout
  Subtractor #(.width(5)) subtractor_1 (.a(register_1_q), .b(5'b00010), .out(subtractor_1_out));  // open: bin, bout
  Subtractor #(.width(5)) subtractor_2 (.a(register_1_q), .b(5'b00001), .out(subtractor_2_out));  // open: bin, bout
  Multiplexer #(.width(5), .enable("false")) multiplexer_1 (
    .in0(register_1_q), .in1(adder_1_out), .out(multiplexer_1_out), .sel(push));
  Multiplexer #(.width(5), .enable("false")) multiplexer_2 (
    .in0(register_1_q), .in1(subtractor_2_out), .out(multiplexer_2_out), .sel(and_3_out));
  RAM #(.addrWidth(5), .dataWidth(16), .databus("bibus")) ram_1 (
    .addr(multiplexer_2_out), .we(multiplexer_3_out), .clk(clk), .din(enter), .dout(reseult));  // open: oe
  Multiplexer #(.enable("false")) multiplexer_3 (.in0(1'b0), .in1(1'b1), .out(multiplexer_3_out), .sel(push));
  Multiplexer #(.width(5), .enable("false")) multiplexer_4 (
    .in0(multiplexer_1_out), .in1(subtractor_2_out), .out(multiplexer_4_out), .sel(and_1_out));
  Multiplexer #(.width(5), .enable("false")) multiplexer_5 (
    .in0(multiplexer_4_out), .in1(adder_1_out), .out(multiplexer_5_out), .sel(and_2_out));
  Register #(.width(5)) register_1 (.D(multiplexer_6_out), .clk(clk), .Q(register_1_q), .clr(reset));  // open: en
  Multiplexer #(.width(5), .enable("false")) multiplexer_6 (
    .in0(multiplexer_5_out), .in1(subtractor_1_out), .out(multiplexer_6_out), .sel(and_3_out));
  Register #(.width(1)) register_2 (.D(and_1_out), .clk(clk), .Q(register_2_q), .clr(reset));  // open: en
  and and_2 (and_2_out, register_2_q, ~and_1_out);  // AND_Gate
  and and_3 (and_3_out, ~register_2_q, and_1_out);  // AND_Gate
endmodule
