// Logisim project stack.circ as structural Verilog: 8 circuits, main circuit main
module main (
  input  CLK,
  input  Reset,
  input  [4:0] ADDR,
  input  Push,
  input  Pointer,
  input  [15:0] mem_data_in,
  output isEmpty,
  output [15:0] peek
);

  wire clock_1_out;

  Clock clock_1 (.out(clock_1_out));
  core core_1 (
    .clk(clock_1_out), .reset(Reset), .aDDR(ADDR), .PUSH(Push), .JMP(Pointer), .data(mem_data_in),
    .isEmpty(isEmpty), .peek(peek));
endmodule

module mux4_2 (
  input  [15:0] Input_data,
  input  [15:0] Alu_data,
  input  [15:0] Bstack_data,
  input  [15:0] Bstored_data,
  input  [1:0] in_sel,
  output [15:0] Out_data
);

  Multiplexer #(.select(2), .width(16), .enable("false")) multiplexer_1 (
    .in0(Input_data), .in1(Alu_data), .in2(Bstack_data), .in3(Bstored_data), .out(Out_data), .sel(in_sel));
endmodule

module ALU (
  input  A_in,
  input  [15:0] inputin,
  input  B_in,
  input  [15:0] Aluin,
  input  C_in,
  input  clk,
  input  reset,
  output [15:0] Alu_out
);

  wire [14:0] adder_1_out, and_1_out, divider_1_out, multiplexer_1_out, multiplexer_2_out, multiplier_1_out,
       negator_1_out, not_1_out, or_1_out, register_1_q, register_2_q, shifter_1_out, shifter_2_out,
       subtractor_1_out, undriven, xor_1_out;
  wire [15:0] multiplexer_3_out, register_3_q;

  Multiplexer #(.width(15), .enable("false")) multiplexer_1 (
    .in0(register_1_q), .in1(inputin[14:0]), .out(multiplexer_1_out), .sel(A_in));
  Multiplexer #(.width(15), .enable("false")) multiplexer_2 (
    .in0(register_2_q), .in1(inputin[14:0]), .out(multiplexer_2_out), .sel(B_in));
  Multiplexer #(.width(16), .enable("false")) multiplexer_3 (
    .in0(register_3_q), .in1(Aluin), .out(multiplexer_3_out), .sel(C_in));
  Register #(.width(15)) register_1 (.D(multiplexer_1_out), .clk(clk), .Q(register_1_q), .clr(reset));  // open: en
  Register #(.width(15)) register_2 (.D(multiplexer_2_out), .clk(clk), .Q(register_2_q), .clr(reset));  // open: en
  Register #(.width(16)) register_3 (.D(multiplexer_3_out), .clk(clk), .Q(register_3_q), .clr(reset));  // open: en
  assign or_1_out = register_1_q | register_2_q;  // OR_Gate or_1, 15 bits wide
  assign xor_1_out = register_1_q ^ register_2_q;  // XOR_Gate xor_1, 15 bits wide
  assign and_1_out = register_1_q & register_2_q;  // AND_Gate and_1, 15 bits wide
  Shifter #(.width(15)) shifter_1 (.in(register_1_q), .\dist (register_2_q[3:0]), .out(shifter_1_out));
  Shifter #(.width(15), .shift("lr")) shifter_2 (.in(register_1_q), .\dist (register_2_q[3:0]), .out(shifter_2_out));
  Adder #(.width(15)) adder_1 (.a(register_1_q), .b(register_2_q), .out(adder_1_out));  // open: cin, cout
  Subtractor #(.width(15)) subtractor_1 (
    .a(register_1_q), .b(register_2_q), .out(subtractor_1_out));  // open: bin, bout
  Multiplier #(.width(15)) multiplier_1 (
    .a(register_1_q), .b(register_2_q), .out(multiplier_1_out));  // open: cin, cout
  Negator #(.width(15)) negator_1 (.in(register_2_q), .out(negator_1_out));
  Divider #(.width(15)) divider_1 (.a(register_1_q), .b(register_2_q), .out(divider_1_out));  // open: upper, rem
  assign not_1_out = ~register_1_q;  // NOT_Gate not_1, 15 bits wide
  Multiplexer #(.select(4), .width(15), .enable("false")) multiplexer_4 (
    .in0(register_1_q), .in1(or_1_out), .in2(xor_1_out), .in3(and_1_out), .in4(shifter_1_out),
    .in5(shifter_2_out), .in6(adder_1_out), .in7(subtractor_1_out), .in8(multiplier_1_out),
    .in9(negator_1_out), .in10(divider_1_out), .in11(not_1_out), .in12(undriven), .in13(undriven),
    .in14(undriven), .in15(undriven), .out(Alu_out[14:0]), .sel(register_3_q[3:0]));

  assign Alu_out[15] = 1'b0;
endmodule

module stack (
  input  push,
  input  pop,
  input  rst,
  input  clk,
  input  [15:0] data_in,
  output [4:0] Pointer,
  output [15:0] Top
);

  wire multiplexer_2_out;
  wire [4:0] adder_1_out, multiplexer_1_out, multiplexer_3_out, multiplexer_4_out, subtractor_1_out;

  Adder #(.width(5)) adder_1 (.a(Pointer), .b(5'b00001), .out(adder_1_out));  // open: cin, cout
  Subtractor #(.width(5)) subtractor_1 (.a(Pointer), .b(5'b00001), .out(subtractor_1_out));  // open: bin, bout
  Multiplexer #(.width(5), .enable("false")) multiplexer_1 (
    .in0(subtractor_1_out), .in1(Pointer), .out(multiplexer_1_out), .sel(push));
  RAM #(.addrWidth(5), .dataWidth(16), .databus("bibus")) ram_1 (
    .addr(multiplexer_1_out), .we(multiplexer_2_out), .clk(clk), .din(data_in), .dout(Top));  // open: oe
  Multiplexer #(.enable("false")) multiplexer_2 (.in0(1'b0), .in1(1'b1), .out(multiplexer_2_out), .sel(push));
  Multiplexer #(.width(5), .enable("false")) multiplexer_3 (
    .in0(Pointer), .in1(adder_1_out), .out(multiplexer_3_out), .sel(push));
  Multiplexer #(.width(5), .enable("false")) multiplexer_4 (
    .in0(multiplexer_3_out), .in1(subtractor_1_out), .out(multiplexer_4_out), .sel(pop));
  Register #(.width(5)) register_1 (.D(multiplexer_4_out), .clk(clk), .Q(Pointer), .clr(rst));  // open: en
endmodule

module data_path (
  input  PushA,
  input  PushB,
  input  PopB,
  input  PopA,
  input  A,
  input  B,
  input  C,
  input  rst,
  input  clk,
  input  [15:0] datain,
  input  [1:0] d_select,
  input  E,
  output [4:0] PointerA,
  output [15:0] Top,
  output [4:0] PointerB,
  output [15:0] Ain,
  output great
);

  wire [15:0] multiplexer_1_out, multiplexer_2_out, register_1_q, register_2_q, stack_1_top, stack_2_top;

  Register #(.width(16)) register_1 (.D(multiplexer_1_out), .clk(clk), .Q(register_1_q), .clr(rst));  // open: en
  Multiplexer #(.width(16), .enable("false")) multiplexer_1 (
    .in0(register_1_q), .in1(stack_2_top), .out(multiplexer_1_out), .sel(C));
  Register #(.width(16)) register_2 (.D(multiplexer_2_out), .clk(clk), .Q(register_2_q), .clr(rst));  // open: en
  Multiplexer #(.width(16), .enable("false")) multiplexer_2 (
    .in0(register_2_q), .in1(stack_2_top), .out(multiplexer_2_out), .sel(E));
  stack stack_1 (.push(PushA), .pop(PopA), .rst(rst), .clk(clk), .data_in(Ain), .Pointer(PointerA), .Top(stack_1_top));
  stack stack_2 (.push(PushB), .pop(PopB), .rst(rst), .clk(clk), .data_in(Ain), .Pointer(PointerB), .Top(stack_2_top));
  Comparator #(.width(16), .mode("unsigned")) comparator_1 (
    .a(register_1_q), .b(register_2_q), .lt(great));  // open: gt, eq
  ALU alu_1 (
    .A_in(A), .inputin(stack_1_top), .B_in(B), .Aluin(stack_2_top), .C_in(C), .clk(clk), .reset(rst),
    .Alu_out(Top));
  mux4_2 mux4_2_1 (
    .Input_data(datain), .Alu_data(Top), .Bstack_data(register_1_q), .Bstored_data(register_2_q),
    .in_sel(d_select), .Out_data(Ain));
endmodule

module control (
  input  [15:0] Ain,
  input  great,
  input  [4:0] PosB,
  input  [4:0] PosA,
  input  [4:0] inpos,
  input  clk,
  input  reset,
  output DONE,
  output [1:0] d_select,
  output pushA,
  output PushB,
  output PopB,
  output PopA,
  output AluA,
  output AluB,
  output AluSel,
  output D
);

  wire and_1_out, and_3_out, and_4_out, and_5_out, and_6_out, and_7_out, and_8_out, and_9_out, and_10_out,
       comparator_1_eq, comparator_1_gt, comparator_1_lt, comparator_2_eq, comparator_3_eq, comparator_4_gt,
       comparator_5_gt, comparator_6_eq, multiplexer_1_out, multiplexer_6_out, multiplexer_9_out,
       multiplexer_10_out, multiplexer_11_out, multiplexer_12_out, multiplexer_13_out, multiplexer_14_out,
       multiplexer_15_out, multiplexer_16_out, multiplexer_17_out, multiplexer_18_out, multiplexer_20_out,
       multiplexer_22_out, multiplexer_23_out, multiplexer_24_out, multiplexer_25_out, multiplexer_26_out,
       multiplexer_27_out, multiplexer_28_out, not_1_out, or_1_out, or_2_out, or_3_out, or_4_out, or_5_out,
       register_3_q, register_4_q, register_5_q, register_6_q, register_7_q, register_8_q, register_9_q,
       register_10_q, register_12_q, register_13_q, register_15_q, undriven;
  wire [1:0] multiplexer_2_out, multiplexer_3_out, multiplexer_4_out, multiplexer_5_out, multiplexer_8_out;
  wire [4:0] adder_1_out, multiplexer_7_out, multiplexer_19_out, register_1_q, subtractor_1_out;

  Comparator #(.width(5)) comparator_1 (
    .a(PosB), .b(5'b00001), .gt(comparator_1_gt), .eq(comparator_1_eq), .lt(comparator_1_lt));
  Comparator #(.width(5)) comparator_2 (.a(PosA), .b(5'b00001), .eq(comparator_2_eq));  // open: gt, lt
  Comparator #(.width(5)) comparator_3 (.a(inpos), .b({5{1'b0}}), .eq(comparator_3_eq));  // open: gt, lt
  and and_1 (and_1_out, comparator_1_lt, comparator_2_eq, comparator_3_eq);
  Subtractor #(.width(5)) subtractor_1 (.a(register_1_q), .b(5'b00001), .out(subtractor_1_out));  // open: bin, bout
  and and_2 (AluSel, ~PopB, register_12_q);  // AND_Gate
  Adder #(.width(5)) adder_1 (.a(register_1_q), .b(5'b00001), .out(adder_1_out));  // open: cin, cout
  Comparator #(.width(5)) comparator_4 (.a(register_1_q), .b(5'b00011), .gt(comparator_4_gt));  // open: eq, lt
  Multiplexer #(.enable("false")) multiplexer_1 (
    .in0(comparator_4_gt), .in1(comparator_5_gt), .out(multiplexer_1_out), .sel(or_1_out));
  Comparator #(.width(5)) comparator_5 (.a(register_1_q), .b(5'b00001), .gt(comparator_5_gt));  // open: eq, lt
  or or_1 (or_1_out, PopB, PopA, register_8_q, register_7_q);
  or or_2 (or_2_out, and_9_out, and_5_out);
  or or_3 (or_3_out, multiplexer_1_out, DONE);
  Multiplexer #(.select(2), .width(2), .enable("false")) multiplexer_2 (
    .in0(2'b10), .in1(2'b11), .in2(2'b00), .in3(2'b00), .out(multiplexer_2_out), .sel(subtractor_1_out[1:0]));
  Multiplexer #(.width(2), .enable("false")) multiplexer_3 (
    .in0(2'b00), .in1(2'b00), .out(multiplexer_3_out), .sel(subtractor_1_out[0]));
  Multiplexer #(.width(2), .enable("false")) multiplexer_4 (
    .in0(multiplexer_3_out), .in1(multiplexer_5_out), .out(multiplexer_4_out), .sel(register_7_q));
  Multiplexer #(.width(2), .enable("false")) multiplexer_5 (
    .in0(2'b01), .in1(2'b11), .out(multiplexer_5_out), .sel(subtractor_1_out[0]));
  or or_4 (or_4_out, register_8_q, register_7_q, register_6_q, register_5_q);
  Multiplexer #(.enable("false")) multiplexer_6 (.in0(1'b0), .in1(1'b1), .out(multiplexer_6_out), .sel(Ain[15]));
  and and_3 (and_3_out, register_10_q, ~register_9_q, ~PushB, ~pushA);  // AND_Gate
  and and_4 (and_4_out, PopA, register_15_q);
  Comparator #(.width(5)) comparator_6 (.a(register_1_q), .b(5'b00010), .eq(comparator_6_eq));  // open: gt, lt
  Multiplexer #(.width(5), .enable("false")) multiplexer_7 (
    .in0(adder_1_out), .in1(5'b00001), .out(multiplexer_7_out), .sel(or_2_out));
  Multiplexer #(.width(2), .enable("false")) multiplexer_8 (
    .in0(multiplexer_2_out), .in1(multiplexer_4_out), .out(multiplexer_8_out), .sel(or_5_out));
  or or_5 (or_5_out, register_7_q, register_8_q);
  Multiplexer #(.enable("false")) multiplexer_9 (.in0(register_3_q), .in1(1'b0), .out(multiplexer_9_out), .sel(PopB));
  Multiplexer #(.enable("false")) multiplexer_10 (
    .in0(register_4_q), .in1(1'b0), .out(multiplexer_10_out), .sel(or_4_out));
  Multiplexer #(.enable("false")) multiplexer_11 (
    .in0(multiplexer_10_out), .in1(1'b1), .out(multiplexer_11_out), .sel(reset));
  Multiplexer #(.enable("false")) multiplexer_12 (
    .in0(register_5_q), .in1(1'b0), .out(multiplexer_12_out), .sel(or_3_out));
  and and_5 (and_5_out, ~register_12_q, great, register_13_q);  // AND_Gate
  Multiplexer #(.enable("false")) multiplexer_13 (
    .in0(register_6_q), .in1(1'b0), .out(multiplexer_13_out), .sel(or_3_out));
  Multiplexer #(.enable("false")) multiplexer_14 (
    .in0(register_7_q), .in1(1'b0), .out(multiplexer_14_out), .sel(or_3_out));
  and and_6 (and_6_out, ~PopA, register_15_q);  // AND_Gate
  Multiplexer #(.enable("false")) multiplexer_15 (
    .in0(register_8_q), .in1(1'b0), .out(multiplexer_15_out), .sel(or_3_out));
  and and_7 (and_7_out, comparator_1_eq, and_3_out);
  not not_1 (not_1_out, multiplexer_6_out);
  Multiplexer #(.enable("false")) multiplexer_16 (.in0(PopB), .in1(1'b0), .out(multiplexer_16_out), .sel(or_3_out));
  and and_8 (and_8_out, and_3_out, comparator_1_gt);
  Multiplexer #(.enable("false")) multiplexer_17 (.in0(PopA), .in1(1'b0), .out(multiplexer_17_out), .sel(and_4_out));
  and and_9 (and_9_out, ~register_12_q, ~great, register_13_q);  // AND_Gate
  Multiplexer #(.enable("false")) multiplexer_18 (.in0(1'b0), .in1(1'b0), .out(multiplexer_18_out), .sel(or_3_out));
  and and_10 (and_10_out, PopA, comparator_6_eq);
  and and_11 (D, comparator_6_eq, PopB);
  Register #(.width(5)) register_1 (.D(multiplexer_19_out), .en(undriven), .clk(clk), .Q(register_1_q), .clr(reset));
  Multiplexer #(.width(5), .enable("false")) multiplexer_19 (
    .in0(multiplexer_7_out), .in1({5{1'b0}}), .out(multiplexer_19_out), .sel(multiplexer_1_out));
  Register #(.width(1)) register_2 (.D(multiplexer_20_out), .clk(clk), .Q(DONE), .clr(reset));  // open: en
  Multiplexer #(.enable("false")) multiplexer_20 (.in0(DONE), .in1(1'b1), .out(multiplexer_20_out), .sel(and_1_out));
  Multiplexer #(.width(2), .enable("false")) multiplexer_21 (
    .in0(multiplexer_8_out), .in1(2'b00), .out(d_select), .sel(register_3_q));
  Register #(.width(1)) register_3 (.D(multiplexer_22_out), .clk(clk), .Q(register_3_q), .clr(reset));  // open: en
  Multiplexer #(.enable("false")) multiplexer_22 (
    .in0(multiplexer_9_out), .in1(1'b1), .out(multiplexer_22_out), .sel(register_4_q));
  Register #(.width(1)) register_4 (.D(multiplexer_11_out), .clk(clk), .Q(register_4_q));  // open: en, clr
  Register #(.width(1)) register_5 (.D(multiplexer_23_out), .clk(clk), .Q(register_5_q), .clr(reset));  // open: en
  Multiplexer #(.enable("false")) multiplexer_23 (
    .in0(multiplexer_12_out), .in1(1'b1), .out(multiplexer_23_out), .sel(and_5_out));
  Register #(.width(1)) register_6 (.D(multiplexer_24_out), .clk(clk), .Q(register_6_q), .clr(reset));  // open: en
  Multiplexer #(.enable("false")) multiplexer_24 (
    .in0(multiplexer_13_out), .in1(1'b1), .out(multiplexer_24_out), .sel(register_4_q));
  Register #(.width(1)) register_7 (.D(multiplexer_25_out), .clk(clk), .Q(register_7_q), .clr(reset));  // open: en
  Multiplexer #(.enable("false")) multiplexer_25 (
    .in0(multiplexer_14_out), .in1(1'b1), .out(multiplexer_25_out), .sel(and_6_out));
  Register #(.width(1)) register_8 (.D(multiplexer_26_out), .clk(clk), .Q(register_8_q), .clr(reset));  // open: en
  Multiplexer #(.enable("false")) multiplexer_26 (
    .in0(multiplexer_15_out), .in1(1'b1), .out(multiplexer_26_out), .sel(and_7_out));
  and and_12 (pushA, not_1_out, or_4_out);
  and and_13 (PushB, or_4_out, multiplexer_6_out);
  Register #(.width(1)) register_9 (.D(pushA), .clk(clk), .Q(register_9_q), .clr(reset));  // open: en
  Register #(.width(1)) register_10 (.D(PushB), .clk(clk), .Q(register_10_q), .clr(reset));  // open: en
  Register #(.width(1)) register_11 (.D(multiplexer_27_out), .clk(clk), .Q(PopB), .clr(reset));  // open: en
  Multiplexer #(.enable("false")) multiplexer_27 (
    .in0(multiplexer_16_out), .in1(1'b1), .out(multiplexer_27_out), .sel(and_8_out));
  Register #(.width(1)) register_12 (.D(PopB), .clk(clk), .Q(register_12_q), .clr(reset));  // open: en
  Register #(.width(1)) register_13 (.D(register_12_q), .clk(clk), .Q(register_13_q), .clr(reset));  // open: en
  Register #(.width(1)) register_14 (.D(multiplexer_28_out), .clk(clk), .Q(PopA), .clr(reset));  // open: en
  Multiplexer #(.enable("false")) multiplexer_28 (
    .in0(multiplexer_17_out), .in1(1'b1), .out(multiplexer_28_out), .sel(and_9_out));
  Register #(.width(1)) register_15 (.D(PopA), .clk(clk), .Q(register_15_q), .clr(reset));  // open: en
  Register #(.width(1)) register_16 (.D(AluB), .clk(clk), .Q(AluA), .clr(reset));  // open: en
  Multiplexer #(.enable("false")) multiplexer_29 (.in0(multiplexer_18_out), .in1(1'b1), .out(AluB), .sel(and_10_out));
endmodule

module core (
  input  clk,
  input  reset,
  input  [4:0] aDDR,
  input  PUSH,
  input  JMP,
  input  [15:0] data,
  output isEmpty,
  output [15:0] peek
);

  wire and_1_out, comparator_1_eq, control_1_alua, control_1_alub, control_1_alusel, control_1_d,
       control_1_popa, control_1_popb, control_1_pusha, control_1_pushb, data_path_1_great, or_1_out;
  wire [1:0] control_1_d_select;
  wire [4:0] acc_in_1_stack_pointer, data_path_1_pointera, data_path_1_pointerb;
  wire [15:0] acc_in_1_peek, data_path_1_ain;

  control control_1 (
    .Ain(data_path_1_ain), .great(data_path_1_great), .PosB(data_path_1_pointerb),
    .PosA(data_path_1_pointera), .inpos(acc_in_1_stack_pointer), .clk(clk), .reset(reset), .DONE(isEmpty),
    .d_select(control_1_d_select), .pushA(control_1_pusha), .PushB(control_1_pushb), .PopB(control_1_popb),
    .PopA(control_1_popa), .AluA(control_1_alua), .AluB(control_1_alub), .AluSel(control_1_alusel),
    .D(control_1_d));
  or or_1 (or_1_out, control_1_pushb, control_1_pusha);
  Comparator #(.width(2), .mode("unsigned")) comparator_1 (
    .a(control_1_d_select), .b(2'b00), .eq(comparator_1_eq));  // open: gt, lt
  and and_1 (and_1_out, or_1_out, comparator_1_eq);
  data_path data_path_1 (
    .PushA(control_1_pusha), .PushB(control_1_pushb), .PopB(control_1_popb), .PopA(control_1_popa),
    .A(control_1_alua), .B(control_1_alub), .C(control_1_alusel), .rst(reset), .clk(clk),
    .datain(acc_in_1_peek), .d_select(control_1_d_select), .E(control_1_d), .PointerA(data_path_1_pointera),
    .Top(peek), .PointerB(data_path_1_pointerb), .Ain(data_path_1_ain), .great(data_path_1_great));
  acc_in acc_in_1 (
    .jump(aDDR), .push(PUSH), .pop(and_1_out), .jmp(JMP), .clk(clk), .inn(data),
    .stack_pointer(acc_in_1_stack_pointer), .peek(acc_in_1_peek));
endmodule

module acc_in (
  input  [4:0] jump,
  input  push,
  input  pop,
  input  jmp,
  input  clk,
  input  [15:0] inn,
  output [4:0] stack_pointer,
  output [15:0] peek
);

  wire multiplexer_4_out, undriven;
  wire [4:0] adder_1_out, multiplexer_1_out, multiplexer_2_out, multiplexer_3_out, subtractor_1_out;

  Adder #(.width(5)) adder_1 (.a(stack_pointer), .b(5'b00001), .out(adder_1_out));  // open: cin, cout
  Subtractor #(.width(5)) subtractor_1 (.a(stack_pointer), .b(5'b00001), .out(subtractor_1_out));  // open: bin, bout
  Multiplexer #(.width(5), .enable("false")) multiplexer_1 (
    .in0(stack_pointer), .in1(adder_1_out), .out(multiplexer_1_out), .sel(push));
  Multiplexer #(.width(5), .enable("false")) multiplexer_2 (
    .in0(multiplexer_1_out), .in1(subtractor_1_out), .out(multiplexer_2_out), .sel(pop));
  Register #(.width(5)) register_1 (.D(multiplexer_3_out), .en(undriven), .clk(clk), .Q(stack_pointer));  // open: clr
  Multiplexer #(.width(5), .enable("false")) multiplexer_3 (
    .in0(multiplexer_2_out), .in1(jump), .out(multiplexer_3_out), .sel(jmp));
  RAM #(.addrWidth(5), .dataWidth(16), .databus("bibus")) ram_1 (
    .addr(multiplexer_3_out), .we(multiplexer_4_out), .clk(clk), .din(inn), .dout(peek));  // open: oe
  Multiplexer #(.enable("false")) multiplexer_4 (.in0(1'b0), .in1(1'b1), .out(multiplexer_4_out), .sel(push));
endmodule
