// Logisim project stackpointer.circ as structural Verilog: 10 circuits, main circuit main
module main (
  input  clk,
  input  reset,
  input  [15:0] mem_data_in,
  output [15:0] mem_data,
  output [10:0] mem_addr,
  output mem_write
);

  core core_1 (
    .clk(clk), .reset(reset), .data_in(mem_data_in), .mem_data(mem_data), .mem_addr(mem_addr),
    .mem_write(mem_write));
endmodule

module mux2_1 (
  input  [15:0] B,
  input  [15:0] A,
  input  selector,
  output [15:0] outt
);

  Multiplexer #(.width(16), .enable("false")) multiplexer_1 (.in0(B), .in1(A), .out(outt), .sel(selector));
endmodule

module mux4_2 (
  input  [15:0] a,
  input  [15:0] b,
  input  [15:0] c,
  input  [15:0] d,
  input  [1:0] SELECTS,
  output [15:0] OUTT
);

  Multiplexer #(.select(2), .width(16), .enable("false")) multiplexer_1 (
    .in0(a), .in1(b), .in2(c), .in3(d), .out(OUTT), .sel(SELECTS));
endmodule

module bufferS (
  input  [15:0] INN,
  input  ENABLE,
  output [15:0] OUTT
);

  assign OUTT = ENABLE ? INN : 16'bz;  // Controlled_Buffer controlled_buffer_1
endmodule

module ALU (
  input  [15:0] tos,
  input  [15:0] nexxt,
  input  [3:0] selectt,
  output [15:0] o_tos,
  output [15:0] o_next
);

  wire comparator_1_eq, comparator_1_gt, comparator_1_lt, comparator_2_eq;
  wire [15:0] adder_1_out, and_1_out, multiplexer_1_out, multiplexer_2_out, multiplexer_3_out,
       multiplier_1_out, not_1_out, or_1_out, subtractor_1_out, undriven, xor_1_out;

  Adder #(.width(16)) adder_1 (.a(tos), .b(nexxt), .out(adder_1_out));  // open: cin, cout
  Subtractor #(.width(16)) subtractor_1 (.a(tos), .b(nexxt), .out(subtractor_1_out));  // open: bin, bout
  Multiplier #(.width(16)) multiplier_1 (.a(tos), .b(nexxt), .out(multiplier_1_out));  // open: cin, cout
  assign and_1_out = tos & nexxt;  // AND_Gate and_1, 16 bits wide
  assign or_1_out = tos | nexxt;  // OR_Gate or_1, 16 bits wide
  assign xor_1_out = tos ^ nexxt;  // XOR_Gate xor_1, 16 bits wide
  Multiplexer #(.width(16), .enable("false")) multiplexer_1 (
    .in0({16{1'b0}}), .in1({16{1'b1}}), .out(multiplexer_1_out), .sel(comparator_1_gt));
  Comparator #(.width(16), .mode("unsigned")) comparator_1 (
    .a(tos), .b(nexxt), .gt(comparator_1_gt), .eq(comparator_1_eq), .lt(comparator_1_lt));
  Multiplexer #(.width(16), .enable("false")) multiplexer_2 (
    .in0({16{1'b0}}), .in1({16{1'b1}}), .out(multiplexer_2_out), .sel(comparator_1_eq));
  Multiplexer #(.width(16), .enable("false")) multiplexer_3 (
    .in0({16{1'b0}}), .in1({16{1'b1}}), .out(multiplexer_3_out), .sel(comparator_1_lt));
  assign not_1_out = ~tos;  // NOT_Gate not_1, 16 bits wide
  Multiplexer #(.select(4), .width(16), .enable("false")) multiplexer_4 (
    .in0(tos), .in1(adder_1_out), .in2(subtractor_1_out), .in3(multiplier_1_out), .in4(undriven),
    .in5(undriven), .in6(and_1_out), .in7(or_1_out), .in8(xor_1_out), .in9(multiplexer_2_out),
    .in10(multiplexer_1_out), .in11(multiplexer_3_out), .in12(not_1_out), .in13(nexxt), .in14(undriven),
    .in15(undriven), .out(o_tos), .sel(selectt));
  Multiplexer #(.width(16), .enable("false")) multiplexer_5 (
    .in0(nexxt), .in1(tos), .out(o_next), .sel(comparator_2_eq));
  Comparator #(.width(4), .mode("unsigned")) comparator_2 (
    .a(selectt), .b(4'b1101), .eq(comparator_2_eq));  // open: gt, lt
endmodule

module stack (
  input  push,
  input  pop,
  input  rst,
  input  clk,
  input  w_next,
  input  w_tos,
  input  [15:0] next_in,
  input  [15:0] top_in,
  output [4:0] next_position,
  output [4:0] tos_position,
  output [15:0] top_out,
  output [15:0] next_out
);

  wire [4:0] adder_1_out, adder_2_out, multiplexer_1_out, multiplexer_2_out, multiplexer_5_out,
       multiplexer_6_out, multiplexer_7_out, multiplexer_8_out, multiplexer_9_out, subtractor_1_out,
       subtractor_2_out;
  wire [15:0] demultiplexer_2_out0, multiplexer_3_out, multiplexer_4_out, ram_1_dout;

  Adder #(.width(5)) adder_1 (.a(next_position), .b(5'b00001), .out(adder_1_out));  // open: cin, cout
  Subtractor #(.width(5)) subtractor_1 (.a(next_position), .b(5'b00001), .out(subtractor_1_out));  // open: bin, bout
  Adder #(.width(5)) adder_2 (.a(tos_position), .b(5'b00001), .out(adder_2_out));  // open: cin, cout
  Subtractor #(.width(5)) subtractor_2 (.a(tos_position), .b(5'b00001), .out(subtractor_2_out));  // open: bin, bout
  RAM #(.addrWidth(5), .dataWidth(16), .databus("bibus")) ram_1 (
    .addr(multiplexer_2_out), .clk(clk), .din(multiplexer_4_out), .dout(ram_1_dout));  // open: we, oe
  Multiplexer #(.width(5), .enable("false")) multiplexer_1 (
    .in1(next_position), .out(multiplexer_1_out), .sel(w_next));  // open: in0
  Multiplexer #(.width(5), .enable("false")) multiplexer_2 (
    .in0(multiplexer_1_out), .in1(tos_position), .out(multiplexer_2_out), .sel(w_tos));
  Multiplexer #(.width(16), .enable("false")) multiplexer_3 (
    .in1(next_in), .out(multiplexer_3_out), .sel(w_next));  // open: in0
  Multiplexer #(.width(16), .enable("false")) multiplexer_4 (
    .in0(multiplexer_3_out), .in1(top_in), .out(multiplexer_4_out), .sel(w_tos));
  Multiplexer #(.width(5), .enable("false")) multiplexer_5 (
    .in0(next_position), .in1(adder_1_out), .out(multiplexer_5_out), .sel(push));
  Multiplexer #(.width(5), .enable("false")) multiplexer_6 (
    .in0(multiplexer_5_out), .in1(subtractor_1_out), .out(multiplexer_6_out), .sel(pop));
  Multiplexer #(.width(5), .enable("false")) multiplexer_7 (
    .in0(tos_position), .in1(adder_2_out), .out(multiplexer_7_out), .sel(push));
  Multiplexer #(.width(5), .enable("false")) multiplexer_8 (
    .in0(multiplexer_7_out), .in1(subtractor_2_out), .out(multiplexer_8_out), .sel(pop));
  Register #(.width(5)) register_1 (.D(multiplexer_9_out), .clk(clk), .Q(next_position));  // open: en, clr
  Multiplexer #(.width(5), .enable("false")) multiplexer_9 (
    .in0(multiplexer_6_out), .in1({5{1'b1}}), .out(multiplexer_9_out), .sel(rst));
  Register #(.width(5)) register_2 (.D(multiplexer_8_out), .clk(clk), .Q(tos_position), .clr(rst));  // open: en
  Demultiplexer #(.width(16), .enable("false")) demultiplexer_1 (
    .out1(top_out), .in(demultiplexer_2_out0), .sel(w_tos));  // open: out0
  Demultiplexer #(.width(16), .enable("false")) demultiplexer_2 (
    .out0(demultiplexer_2_out0), .out1(next_out), .in(ram_1_dout), .sel(w_next));
endmodule

module data_path (
  input  data_push,
  input  data_pop,
  input  rst,
  input  clk,
  input  dw_next,
  input  [3:0] alu_select,
  input  dw_tos,
  input  [15:0] r_in,
  input  r_select,
  input  r_push,
  input  r_pop,
  input  rw_tos,
  input  [1:0] d_select,
  input  w_mem,
  input  [15:0] mem_data,
  output [10:0] new_addr,
  output [4:0] new_instr,
  output tos_or,
  output [15:0] r_tos
);

  wire not_1_out;
  wire [15:0] alu_1_o_next, alu_1_o_tos, buffers_1_outt, mux2_1_1_outt, mux4_2_1_outt, stack_1_next_out;

  stack stack_1 (
    .push(data_push), .pop(data_pop), .rst(rst), .clk(clk), .w_next(dw_next), .w_tos(dw_tos),
    .next_in(alu_1_o_next), .top_in(mux4_2_1_outt), .top_out({new_instr, new_addr}),
    .next_out(stack_1_next_out));  // open: next_position, tos_position
  stack stack_2 (
    .push(r_push), .pop(r_pop), .rst(rst), .clk(clk), .w_next(1'b0), .w_tos(rw_tos), .top_in(mux2_1_1_outt),
    .top_out(r_tos));  // open: next_in, next_position, tos_position, next_out
  Comparator #(.width(16), .mode("unsigned")) comparator_1 (
    .a({new_instr, new_addr}), .b({16{1'b0}}), .gt(tos_or));  // open: eq, lt
  ALU alu_1 (
    .tos({new_instr, new_addr}), .nexxt(stack_1_next_out), .selectt(alu_select), .o_tos(alu_1_o_tos),
    .o_next(alu_1_o_next));
  mux2_1 mux2_1_1 (.B({new_instr, new_addr}), .A(r_in), .selector(r_select), .outt(mux2_1_1_outt));
  mux4_2 mux4_2_1 (
    .a(buffers_1_outt), .b(r_tos), .c(alu_1_o_tos), .d(stack_1_next_out), .SELECTS(d_select),
    .OUTT(mux4_2_1_outt));
  bufferS buffers_1 (.INN({new_instr, new_addr}), .ENABLE(w_mem), .OUTT(buffers_1_outt));
  assign buffers_1_outt = not_1_out ? mem_data : 16'bz;  // Controlled_Buffer controlled_buffer_1
  not not_1 (not_1_out, w_mem);
endmodule

module control (
  input  [4:0] new_instr,
  input  [15:0] r_in,
  input  [10:0] new_addr,
  input  tos_or,
  input  clk,
  input  reset,
  output double,
  output [4:0] instruction,
  output [3:0] alu_select,
  output [15:0] r_out,
  output [1:0] d_select,
  output data_pop,
  output data_push,
  output dw_next,
  output r_pop,
  output dw_tos,
  output mem_write,
  output [10:0] load_return,
  output [10:0] next_addr,
  output [10:0] mem_addr,
  output r_push,
  output r_select,
  output rw_tos
);

  wire and_1_out, and_2_out, and_3_out, and_4_out, and_5_out, and_6_out, and_7_out, clock_1_out,
       comparator_1_eq, comparator_2_eq, comparator_3_gt, comparator_4_eq, comparator_5_eq, comparator_6_eq,
       comparator_7_gt, comparator_8_lt, comparator_9_gt, comparator_10_lt, comparator_11_gt,
       comparator_12_gt, comparator_13_gt, comparator_14_gt, comparator_15_gt, comparator_16_gt,
       comparator_17_gt, comparator_18_lt, comparator_19_eq, comparator_20_gt, comparator_20_lt,
       multiplexer_4_out, multiplexer_10_out, multiplexer_11_out, multiplexer_12_out, multiplexer_13_out,
       multiplexer_14_out, multiplexer_15_out, multiplexer_16_out, multiplexer_17_out, multiplexer_18_out,
       multiplexer_19_out, multiplexer_20_out, multiplexer_21_out, multiplexer_26_out, multiplexer_27_out,
       multiplexer_28_out, multiplexer_29_out, multiplexer_30_out, multiplexer_31_out, not_1_out, not_2_out,
       not_3_out, not_4_out, not_5_out, not_6_out, not_7_out, not_8_out, not_9_out, not_10_out, not_11_out,
       not_12_out, not_13_out, not_14_out, not_15_out, or_1_out, or_2_out, or_3_out, or_4_out, or_5_out,
       or_6_out;
  wire [1:0] multiplexer_8_out, multiplexer_9_out;
  wire [3:0] multiplexer_6_out, subtractor_1_out;
  wire [4:0] multiplexer_5_out;
  wire [10:0] adder_1_out, adder_2_out, adder_3_out, multiplexer_1_out, multiplexer_2_out, multiplexer_3_out,
       multiplexer_22_out, multiplexer_23_out, multiplexer_24_out, multiplexer_25_out;
  wire [15:0] multiplexer_7_out;

  Adder #(.width(11)) adder_1 (.a(11'h1), .b(r_in[10:0]), .out(adder_1_out));  // open: cin, cout
  Comparator #(.width(5), .mode("unsigned")) comparator_1 (
    .a(instruction), .b(5'b11101), .eq(comparator_1_eq));  // open: gt, lt
  Comparator #(.width(5), .mode("unsigned")) comparator_2 (
    .a(instruction), .b(5'b11100), .eq(comparator_2_eq));  // open: gt, lt
  Multiplexer #(.width(11), .enable("false")) multiplexer_1 (
    .in0(next_addr), .in1(adder_1_out), .out(multiplexer_1_out), .sel(comparator_1_eq));
  Multiplexer #(.width(11), .enable("false")) multiplexer_2 (
    .in0(multiplexer_1_out), .in1(r_in[10:0]), .out(multiplexer_2_out), .sel(comparator_2_eq));
  Comparator #(.width(5), .mode("unsigned")) comparator_3 (
    .a(instruction), .b(5'b01000), .gt(comparator_3_gt));  // open: eq, lt
  Comparator #(.width(5), .mode("unsigned")) comparator_4 (
    .a(instruction), .b(5'b11001), .eq(comparator_4_eq));  // open: gt, lt
  Comparator #(.width(5), .mode("unsigned")) comparator_5 (
    .a(instruction), .b(5'b11011), .eq(comparator_5_eq));  // open: gt, lt
  Comparator #(.width(5), .mode("unsigned")) comparator_6 (
    .a(instruction), .b(5'b11010), .eq(comparator_6_eq));  // open: gt, lt
  Comparator #(.width(5), .mode("unsigned")) comparator_7 (
    .a(instruction), .b(5'b10100), .gt(comparator_7_gt));  // open: eq, lt
  Comparator #(.width(5), .mode("unsigned")) comparator_8 (
    .a(instruction), .b(5'b10101), .lt(comparator_8_lt));  // open: gt, eq
  Comparator #(.width(5), .mode("unsigned")) comparator_9 (
    .a(instruction), .b(5'b00100), .gt(comparator_9_gt));  // open: eq, lt
  not not_1 (not_1_out, double);
  and and_1 (and_1_out, comparator_4_eq, ~tos_or);  // AND_Gate
  and and_2 (and_2_out, tos_or, or_1_out);
  or or_1 (or_1_out, comparator_5_eq, comparator_6_eq);
  Comparator #(.width(5), .mode("unsigned")) comparator_10 (
    .a(instruction), .b(5'b00101), .lt(comparator_10_lt));  // open: gt, eq
  not not_2 (not_2_out, double);
  Comparator #(.width(5), .mode("unsigned")) comparator_11 (
    .a(instruction), .b(5'b00100), .gt(comparator_11_gt));  // open: eq, lt
  Comparator #(.width(5), .mode("unsigned")) comparator_12 (
    .a(instruction), .b(5'b00001), .gt(comparator_12_gt));  // open: eq, lt
  Comparator #(.width(5), .mode("unsigned")) comparator_13 (
    .a(instruction), .b(5'b01000), .gt(comparator_13_gt));  // open: eq, lt
  Comparator #(.width(5), .mode("unsigned")) comparator_14 (
    .a(instruction), .b(5'b10101), .gt(comparator_14_gt));  // open: eq, lt
  Comparator #(.width(5), .mode("unsigned")) comparator_15 (
    .a(instruction), .b({5{1'b0}}), .gt(comparator_15_gt));  // open: eq, lt
  Comparator #(.width(5), .mode("unsigned")) comparator_16 (
    .a(instruction), .b(5'b00010), .gt(comparator_16_gt));  // open: eq, lt
  Comparator #(.width(5), .mode("unsigned")) comparator_17 (
    .a(instruction), .b(5'b00001), .gt(comparator_17_gt));  // open: eq, lt
  Multiplexer #(.width(11), .enable("false")) multiplexer_3 (
    .in0(multiplexer_2_out), .in1(new_addr), .out(multiplexer_3_out), .sel(or_2_out));
  or or_2 (or_2_out, and_7_out, and_6_out);
  Adder #(.width(11)) adder_2 (.a(mem_addr), .b({11{1'b1}}), .out(adder_2_out));  // open: cin, cout
  Comparator #(.width(5), .mode("unsigned")) comparator_18 (
    .a(instruction), .b(5'b00101), .lt(comparator_18_lt));  // open: gt, eq
  Comparator #(.width(5), .mode("unsigned")) comparator_19 (
    .a(instruction), .b(5'b11001), .eq(comparator_19_eq));  // open: gt, lt
  Comparator #(.width(5), .mode("unsigned")) comparator_20 (
    .a(instruction), .b(5'b11001), .gt(comparator_20_gt), .lt(comparator_20_lt));  // open: eq
  or or_3 (or_3_out, and_7_out, and_6_out, and_3_out);
  and and_3 (and_3_out, comparator_3_gt, comparator_20_lt);
  or or_4 (or_4_out, and_6_out, and_7_out);
  or or_5 (or_5_out, and_7_out, and_6_out, and_4_out);
  and and_4 (and_4_out, comparator_7_gt, comparator_20_lt);
  Multiplexer #(.enable("false")) multiplexer_4 (.in0(1'b0), .in1(1'b1), .out(multiplexer_4_out), .sel(not_3_out));
  not not_3 (not_3_out, double);
  Multiplexer #(.width(5), .enable("false")) multiplexer_5 (
    .in0(instruction), .in1(new_instr), .out(multiplexer_5_out), .sel(not_4_out));
  not not_4 (not_4_out, double);
  Multiplexer #(.width(4), .enable("false")) multiplexer_6 (
    .in0(alu_select), .in1(subtractor_1_out), .out(multiplexer_6_out), .sel(and_5_out));
  Subtractor #(.width(4)) subtractor_1 (.a(instruction[3:0]), .b(4'b0100), .out(subtractor_1_out));  // open: bin, bout
  and and_5 (and_5_out, comparator_8_lt, not_1_out, comparator_9_gt);
  Multiplexer #(.width(16), .enable("false")) multiplexer_7 (
    .in0(r_out), .in1({{5{1'b0}}, mem_addr}), .out(multiplexer_7_out), .sel(or_6_out));
  or or_6 (or_6_out, and_1_out, and_2_out);
  Multiplexer #(.width(2), .enable("false")) multiplexer_8 (
    .in0(d_select), .in1(multiplexer_9_out), .out(multiplexer_8_out), .sel(not_2_out));
  Multiplexer #(.width(2), .enable("false")) multiplexer_9 (
    .in0(2'b01), .in1(2'b11), .out(multiplexer_9_out), .sel(comparator_10_lt));
  Multiplexer #(.enable("false")) multiplexer_10 (
    .in0(data_pop), .in1(multiplexer_11_out), .out(multiplexer_10_out), .sel(not_5_out));
  Multiplexer #(.enable("false")) multiplexer_11 (
    .in0(1'b1), .in1(1'b0), .out(multiplexer_11_out), .sel(comparator_11_gt));
  not not_5 (not_5_out, double);
  Multiplexer #(.enable("false")) multiplexer_12 (
    .in0(data_push), .in1(multiplexer_13_out), .out(multiplexer_12_out), .sel(not_6_out));
  Multiplexer #(.enable("false")) multiplexer_13 (
    .in0(1'b0), .in1(1'b1), .out(multiplexer_13_out), .sel(comparator_12_gt));
  not not_6 (not_6_out, double);
  Multiplexer #(.enable("false")) multiplexer_14 (
    .in0(dw_next), .in1(multiplexer_15_out), .out(multiplexer_14_out), .sel(not_7_out));
  Multiplexer #(.enable("false")) multiplexer_15 (
    .in0(1'b0), .in1(1'b1), .out(multiplexer_15_out), .sel(comparator_13_gt));
  not not_7 (not_7_out, double);
  Multiplexer #(.enable("false")) multiplexer_16 (
    .in0(r_pop), .in1(multiplexer_17_out), .out(multiplexer_16_out), .sel(not_8_out));
  Multiplexer #(.enable("false")) multiplexer_17 (
    .in0(1'b0), .in1(1'b1), .out(multiplexer_17_out), .sel(comparator_14_gt));
  not not_8 (not_8_out, double);
  Multiplexer #(.enable("false")) multiplexer_18 (
    .in0(dw_tos), .in1(multiplexer_19_out), .out(multiplexer_18_out), .sel(not_9_out));
  Multiplexer #(.enable("false")) multiplexer_19 (
    .in0(1'b0), .in1(1'b1), .out(multiplexer_19_out), .sel(comparator_15_gt));
  not not_9 (not_9_out, double);
  Multiplexer #(.enable("false")) multiplexer_20 (
    .in0(mem_write), .in1(multiplexer_21_out), .out(multiplexer_20_out), .sel(not_10_out));
  Multiplexer #(.enable("false")) multiplexer_21 (
    .in0(1'b0), .in1(1'b1), .out(multiplexer_21_out), .sel(comparator_16_gt));
  not not_10 (not_10_out, double);
  Multiplexer #(.width(11), .enable("false")) multiplexer_22 (
    .in0(load_return), .in1(multiplexer_23_out), .out(multiplexer_22_out), .sel(not_11_out));
  Multiplexer #(.width(11), .enable("false")) multiplexer_23 (
    .in0({11{1'b0}}), .in1(mem_addr), .out(multiplexer_23_out), .sel(comparator_17_gt));
  not not_11 (not_11_out, double);
  Adder #(.width(11)) adder_3 (.a(load_return), .b(11'h1), .out(adder_3_out));  // open: cin, cout
  Multiplexer #(.width(11), .enable("false")) multiplexer_24 (
    .in0(adder_3_out), .in1(multiplexer_25_out), .out(multiplexer_24_out), .sel(not_12_out));
  Multiplexer #(.width(11), .enable("false")) multiplexer_25 (
    .in0(multiplexer_3_out), .in1(adder_2_out), .out(multiplexer_25_out), .sel(comparator_18_lt));
  not not_12 (not_12_out, double);
  and and_6 (and_6_out, ~tos_or, comparator_19_eq);  // AND_Gate
  and and_7 (and_7_out, tos_or, comparator_20_gt);
  Multiplexer #(.enable("false")) multiplexer_26 (
    .in0(r_push), .in1(multiplexer_27_out), .out(multiplexer_26_out), .sel(not_13_out));
  Multiplexer #(.enable("false")) multiplexer_27 (.in0(1'b0), .in1(1'b1), .out(multiplexer_27_out), .sel(or_3_out));
  not not_13 (not_13_out, double);
  Multiplexer #(.enable("false")) multiplexer_28 (
    .in0(r_select), .in1(multiplexer_29_out), .out(multiplexer_28_out), .sel(not_14_out));
  Multiplexer #(.enable("false")) multiplexer_29 (.in0(1'b0), .in1(1'b1), .out(multiplexer_29_out), .sel(or_4_out));
  not not_14 (not_14_out, double);
  Multiplexer #(.enable("false")) multiplexer_30 (
    .in0(rw_tos), .in1(multiplexer_31_out), .out(multiplexer_30_out), .sel(not_15_out));
  Multiplexer #(.enable("false")) multiplexer_31 (.in0(1'b0), .in1(1'b1), .out(multiplexer_31_out), .sel(or_5_out));
  not not_15 (not_15_out, double);
  Clock clock_1 (.out(clock_1_out));
  D_Flip_Flop d_ff_1 (.D(multiplexer_4_out), .clk(clock_1_out), .Q(double), .reset(reset));  // open: Qn, preset
  Register #(.width(5)) register_1 (
    .D(multiplexer_5_out), .clk(clock_1_out), .Q(instruction), .clr(reset));  // open: en
  Register #(.width(4)) register_2 (.D(multiplexer_6_out), .clk(clock_1_out), .Q(alu_select), .clr(reset));  // open: en
  Register #(.width(16)) register_3 (.D(multiplexer_7_out), .clk(clock_1_out), .Q(r_out), .clr(reset));  // open: en
  Register #(.width(2)) register_4 (.D(multiplexer_8_out), .clk(clock_1_out), .Q(d_select), .clr(reset));  // open: en
  D_Flip_Flop d_ff_2 (.D(multiplexer_10_out), .clk(clock_1_out), .Q(data_pop), .reset(reset));  // open: Qn, preset
  D_Flip_Flop d_ff_3 (.D(multiplexer_12_out), .clk(clock_1_out), .Q(data_push), .reset(reset));  // open: Qn, preset
  D_Flip_Flop d_ff_4 (.D(multiplexer_14_out), .clk(clock_1_out), .Q(dw_next), .reset(reset));  // open: Qn, preset
  D_Flip_Flop d_ff_5 (.D(multiplexer_16_out), .clk(clock_1_out), .Q(r_pop), .reset(reset));  // open: Qn, preset
  D_Flip_Flop d_ff_6 (.D(multiplexer_18_out), .clk(clock_1_out), .Q(dw_tos), .reset(reset));  // open: Qn, preset
  D_Flip_Flop d_ff_7 (.D(multiplexer_20_out), .clk(clock_1_out), .Q(mem_write), .reset(reset));  // open: Qn, preset
  Register #(.width(11)) register_5 (
    .D(multiplexer_22_out), .clk(clock_1_out), .Q(load_return), .clr(reset));  // open: en
  Register #(.width(11)) register_6 (
    .D(multiplexer_24_out), .clk(clock_1_out), .Q(next_addr), .clr(reset));  // open: en
  Register #(.width(11)) register_7 (.D(next_addr), .clk(clock_1_out), .Q(mem_addr), .clr(reset));  // open: en
  D_Flip_Flop d_ff_8 (.D(multiplexer_26_out), .clk(clock_1_out), .Q(r_push), .reset(reset));  // open: Qn, preset
  D_Flip_Flop d_ff_9 (.D(multiplexer_28_out), .clk(clock_1_out), .Q(r_select), .reset(reset));  // open: Qn, preset
  D_Flip_Flop d_ff_10 (.D(multiplexer_30_out), .clk(clock_1_out), .Q(rw_tos), .reset(reset));  // open: Qn, preset
endmodule

module control_top (
  input  [4:0] new_instr,
  input  [15:0] r_in,
  input  [10:0] new_addr,
  input  tos_or,
  input  clk,
  input  reset,
  output [3:0] alu_select,
  output [15:0] r_out,
  output [1:0] d_select,
  output data_pop,
  output data_push,
  output dw_next,
  output r_pop,
  output dw_tos,
  output mem_write,
  output [10:0] mem_addr,
  output r_push,
  output r_select,
  output rw_tos
);

  control control_1 (
    .new_instr(new_instr), .r_in(r_in), .new_addr(new_addr), .tos_or(tos_or), .clk(clk), .reset(reset),
    .alu_select(alu_select), .r_out(r_out), .d_select(d_select), .data_pop(data_pop), .data_push(data_push),
    .dw_next(dw_next), .r_pop(r_pop), .dw_tos(dw_tos), .mem_write(mem_write), .next_addr(mem_addr),
    .r_push(r_push), .r_select(r_select), .rw_tos(rw_tos));  // open: double, instruction, load_return, mem_addr
endmodule

module core (
  input  clk,
  input  reset,
  input  [15:0] data_in,
  output [15:0] mem_data,
  output [10:0] mem_addr,
  output mem_write
);

  wire control_top_1_data_pop, control_top_1_data_push, control_top_1_dw_next, control_top_1_dw_tos,
       control_top_1_r_pop, control_top_1_r_push, control_top_1_r_select, control_top_1_rw_tos,
       data_path_1_tos_or, not_1_out;
  wire [1:0] control_top_1_d_select;
  wire [3:0] control_top_1_alu_select;
  wire [15:0] control_top_1_r_out, data_path_1_r_tos;

  not not_1 (not_1_out, clk);
  control_top control_top_1 (
    .new_instr(mem_data[15:11]), .r_in(data_path_1_r_tos), .new_addr(mem_data[10:0]),
    .tos_or(data_path_1_tos_or), .clk(not_1_out), .reset(reset), .alu_select(control_top_1_alu_select),
    .r_out(control_top_1_r_out), .d_select(control_top_1_d_select), .data_pop(control_top_1_data_pop),
    .data_push(control_top_1_data_push), .dw_next(control_top_1_dw_next), .r_pop(control_top_1_r_pop),
    .dw_tos(control_top_1_dw_tos), .mem_write(mem_write), .mem_addr(mem_addr), .r_push(control_top_1_r_push),
    .r_select(control_top_1_r_select), .rw_tos(control_top_1_rw_tos));
  data_path data_path_1 (
    .data_push(control_top_1_data_push), .data_pop(control_top_1_data_pop), .rst(reset), .clk(clk),
    .dw_next(control_top_1_dw_next), .alu_select(control_top_1_alu_select), .dw_tos(control_top_1_dw_tos),
    .r_in(control_top_1_r_out), .r_select(control_top_1_r_push), .r_push(control_top_1_r_select),
    .r_pop(control_top_1_r_pop), .rw_tos(control_top_1_rw_tos), .d_select(control_top_1_d_select),
    .w_mem(mem_write), .mem_data(data_in), .new_addr(mem_data[10:0]), .new_instr(mem_data[15:11]),
    .tos_or(data_path_1_tos_or), .r_tos(data_path_1_r_tos));
endmodule
